# Fritzing sketch PyBrewer (saved by Fritzing 0.9.3b)

parts:
  PI_Zero = Raspberry Pi Zero
  R1 = Resistor [tolerance=±5% resistance=220 package=THT]
  Pump_Relay = RELAY-SOLIDSTATE [package=relay-s108t02]
  Coolant_Probe = DS18B20 1-Wire Temperature Sensor [part_number=DS18B20]
  Wort_Probe = DS18B20 1-Wire Temperature Sensor [part_number=DS18B20]
  Heater_Relay = RELAY-SOLIDSTATE [package=relay-s108t02]
  Water_Pump = mystery part, 2 pins [chip_label=?]
  Water_Heater = mystery part, 2 pins [chip_label=?]
  Power_Supply = AC Power [voltage=220 frequency=60]

nets:
  VDD: PI_Zero.pin_1, PI_Zero.pin_17, Coolant_Probe.VDD, Wort_Probe.VDD
  N1: PI_Zero.pin_8, Pump_Relay.T2
  N2: PI_Zero.pin_10, R1.Pin_0, Coolant_Probe.DQ
  N3: PI_Zero.pin_12, Heater_Relay.T2
  GND: PI_Zero.pin_14, PI_Zero.pin_34, Pump_Relay.T1, Coolant_Probe.GND, Wort_Probe.GND, Heater_Relay.T1
  N4: Pump_Relay.+, Water_Pump.pin1
  N5: Pump_Relay.-, Heater_Relay.-, Power_Supply.V-
  N6: Heater_Relay.+, Water_Heater.pin1
  N7: Water_Pump.pin2, Water_Heater.pin2, Power_Supply.V+
